// Logisim project control_logic.circ as structural Verilog: 1 circuit, main circuit control_logic
module control_logic (
  input  [31:0] inst,
  input  BrEq,
  input  BrLt,
  output PCSel,
  output RegWEn,
  output [2:0] ImmSel,
  output BrUn,
  output ASel,
  output BSel,
  output [3:0] ALUSel,
  output MemRW,
  output [1:0] WBSel,
  output CSRSel,
  output CSRWen
);

  wire and_1_out, and_2_out, and_3_out, and_4_out, and_21_out, and_22_out, and_31_out, and_32_out,
       and_33_out, and_34_out, and_35_out, and_36_out, inst2not, inst3not, inst4not, inst5not, inst6not,
       inst12not, inst13not, inst14not, inst25not, inst30not, isBeq, isBge, isBgeu, isBlt, isBltu, isBne,
       isItype, isJalr_out, isNotRType, isRisAdd, isRisAnd, isRisMul, isRisMulh, isRisMulhu, isRisOr,
       isRisSll, isRisSlt, isRisSra, isRisSrl, isRisSub, isRisXor, isRtype, isSBtype, isUJtype, isUtype,
       not_13_out, not_14_out, not_15_out, or_6_out, or_7_out, WBALU, WBMem, WBPCplus4;
  wire [1:0] demultiplexer_19_out1, demultiplexer_20_out1, demultiplexer_21_out1;
  wire [2:0] immSelI, immSelR, immSelS, immSelSB, immSelU, immSelUJ;
  wire [3:0] RtypeSel, SelAdd, SelAnd, SelMul, SelMulh, SelMulhu, SelOr, SelSll, SelSlt, SelSra, SelSrl,
       SelSub, SelXor;

  Demultiplexer #(.enable("false"), .width(4)) demultiplexer_1 (
    .out1(SelAdd), .in(4'b0000), .sel(isRisAdd));  // open: out0
  Demultiplexer #(.enable("false"), .width(4)) demultiplexer_2 (
    .out1(SelSub), .in(4'b1100), .sel(isRisSub));  // open: out0
  Demultiplexer #(.enable("false"), .width(4)) demultiplexer_3 (
    .out1(SelSll), .in(4'b0110), .sel(isRisSll));  // open: out0
  Demultiplexer #(.enable("false"), .width(3)) demultiplexer_4 (
    .out1(immSelI), .in(3'b000), .sel(isItype));  // open: out0
  and and_1 (and_1_out, inst2not, inst3not, inst4not, inst5not, inst6not);
  and and_2 (and_2_out, inst2not, inst3not, inst[4], inst5not, inst6not);
  and and_3 (and_3_out, inst[2], inst3not, inst4not, inst[5], inst[6]);
  and and_4 (and_4_out, inst2not, inst3not, inst[4], inst[5], inst[6]);
  and and_5 (isSBtype, inst2not, inst3not, inst4not, inst[5], inst[6]);
  and and_6 (isRisAdd, inst12not, inst13not, inst14not, inst30not);
  and and_7 (isRisSub, inst12not, inst13not, inst14not, inst[30]);
  and and_8 (isRisSll, inst[12], inst13not, inst14not, inst30not);
  not not_1 (inst2not, inst[2]);
  not not_2 (inst3not, inst[3]);
  not not_3 (inst4not, inst[4]);
  not not_4 (inst5not, inst[5]);
  not not_5 (inst6not, inst[6]);
  not not_6 (inst12not, inst[12]);
  not not_7 (inst13not, inst[13]);
  not not_8 (inst14not, inst[14]);
  not not_9 (inst30not, inst[30]);
  Demultiplexer #(.enable("false"), .width(3)) demultiplexer_5 (
    .out1(immSelS), .in(3'b001), .sel(MemRW));  // open: out0
  Demultiplexer #(.enable("false"), .width(4)) demultiplexer_6 (
    .out1(SelSlt), .in(4'b0111), .sel(isRisSlt));  // open: out0
  Demultiplexer #(.enable("false"), .width(4)) demultiplexer_7 (
    .out1(SelXor), .in(4'b0011), .sel(isRisXor));  // open: out0
  Demultiplexer #(.enable("false"), .width(4)) demultiplexer_8 (
    .out1(SelSrl), .in(4'b0100), .sel(isRisSrl));  // open: out0
  or or_1 (isItype, and_1_out, and_2_out, and_3_out, and_4_out);
  Demultiplexer #(.enable("false"), .width(3)) demultiplexer_9 (
    .out1(immSelSB), .in(3'b010), .sel(isSBtype));  // open: out0
  Demultiplexer #(.enable("false"), .width(4)) demultiplexer_10 (
    .out1(SelSra), .in(4'b0101), .sel(isRisSra));  // open: out0
  Demultiplexer #(.enable("false"), .width(4)) demultiplexer_11 (
    .out1(SelOr), .in(4'b0010), .sel(isRisOr));  // open: out0
  Demultiplexer #(.enable("false"), .width(4)) demultiplexer_12 (
    .out1(SelAnd), .in(4'b0001), .sel(isRisAnd));  // open: out0
  and and_9 (isRisSlt, inst12not, inst[13], inst14not, inst30not);
  and and_10 (isRisXor, inst12not, inst13not, inst[14], inst30not);
  and and_11 (isRisSrl, inst[12], inst13not, inst[14], inst30not);
  and and_12 (BrUn, inst[13], isSBtype);
  Demultiplexer #(.enable("false"), .width(3)) demultiplexer_13 (
    .out1(immSelU), .in(3'b011), .sel(isUtype));  // open: out0
  Demultiplexer #(.enable("false"), .width(4)) demultiplexer_14 (
    .out1(SelMul), .in(4'b1010), .sel(isRisMul));  // open: out0
  Demultiplexer #(.enable("false"), .width(4)) demultiplexer_15 (
    .out1(SelMulh), .in(4'b1110), .sel(isRisMulh));  // open: out0
  Demultiplexer #(.enable("false"), .width(4)) demultiplexer_16 (
    .out1(SelMulhu), .in(4'b1011), .sel(isRisMulhu));  // open: out0
  not not_10 (inst25not, inst[25]);
  and and_13 (MemRW, inst2not, inst3not, inst4not, inst[5], inst6not);
  Demultiplexer #(.enable("false"), .width(3)) demultiplexer_17 (
    .out1(immSelUJ), .in(3'b100), .sel(isUJtype));  // open: out0
  and and_14 (isRisSra, inst[12], inst13not, inst[14], inst[30]);
  and and_15 (isRisOr, inst12not, inst[13], inst[14], inst30not);
  and and_16 (isRisAnd, inst[12], inst[13], inst[14], inst30not);
  Demultiplexer #(.enable("false"), .width(3)) demultiplexer_18 (
    .out1(immSelR), .in(3'b101), .sel(isRtype));  // open: out0
  assign RtypeSel = SelAdd | SelSub | SelSll | SelSlt | SelXor | SelSrl | SelSra | SelOr | SelAnd | SelMul | SelMulh | SelMulhu;  // OR_Gate or_2, 4 bits wide
  and and_17 (isSBtype, inst2not, inst3not, inst4not, inst[5], inst[6]);
  or or_3 (ASel, isSBtype, isUtype, isUJtype);
  and and_18 (isRisMul, inst12not, inst13not, inst14not, inst[25]);
  and and_19 (isRisMulh, inst[12], inst13not, inst14not, inst[25]);
  and and_20 (isRisMulhu, inst[12], inst[13], inst14not, inst[25]);
  not not_11 (isNotRType, isRtype);
  Multiplexer #(.enable("false"), .width(4)) multiplexer_1 (
    .in0(RtypeSel), .in1(4'b0000), .out(ALUSel), .sel(isNotRType));
  not not_12 (BSel, isRtype);
  assign ImmSel = immSelI | immSelS | immSelSB | immSelU | immSelUJ | immSelR;  // OR_Gate or_4, 3 bits wide
  and and_21 (and_21_out, inst[2], inst3not, inst[4], inst5not, inst6not);
  and and_22 (and_22_out, inst[2], inst3not, inst[4], inst[5], inst6not);
  or or_5 (isUtype, and_21_out, and_22_out);
  and and_23 (isBeq, inst12not, inst13not, inst14not);
  and and_24 (isBne, inst12not, inst13not, inst[14]);
  and and_25 (isBlt, inst[12], inst13not, inst14not);
  and and_26 (isBge, inst[12], inst13not, inst[14]);
  and and_27 (isBltu, inst[12], inst[13], inst14not);
  and and_28 (isBgeu, inst[12], inst[13], inst[14]);
  and and_29 (isUJtype, inst[2], inst[3], inst4not, inst[5], inst[6]);
  not not_13 (not_13_out, BrEq);
  not not_14 (not_14_out, BrLt);
  not not_15 (not_15_out, BrLt);
  and and_30 (isRtype, inst2not, inst3not, inst[4], inst[5], inst6not);
  and and_31 (and_31_out, isBeq, isSBtype, BrEq);
  and and_32 (and_32_out, isBne, isSBtype, not_13_out);
  and and_33 (and_33_out, isBlt, isSBtype, BrLt);
  or or_6 (or_6_out, BrEq, not_14_out);
  and and_34 (and_34_out, isBltu, isSBtype, BrLt);
  or or_7 (or_7_out, BrEq, not_15_out);
  or or_8 (RegWEn, isRtype, isItype, isUtype, isUJtype);
  and and_35 (and_35_out, isBge, isSBtype, or_6_out);
  and and_36 (and_36_out, isBgeu, isSBtype, or_7_out);
  or or_9 (PCSel, and_31_out, and_32_out, and_33_out, and_35_out, and_34_out, and_36_out);
  Demultiplexer #(.enable("false"), .width(2)) demultiplexer_19 (
    .out1(demultiplexer_19_out1), .in(2'b00), .sel(WBMem));  // open: out0
  Demultiplexer #(.enable("false"), .width(2)) demultiplexer_20 (
    .out1(demultiplexer_20_out1), .in(2'b01), .sel(WBALU));  // open: out0
  Demultiplexer #(.enable("false"), .width(2)) demultiplexer_21 (
    .out1(demultiplexer_21_out1), .in(2'b10), .sel(WBPCplus4));  // open: out0
  xnor xnor_1 (WBALU, WBMem, WBPCplus4);
  and isLw (WBMem, inst2not, inst3not, inst4not, inst5not, inst6not);
  and isJalr (isJalr_out, inst[2], inst3not, inst4not, inst[5], inst[6]);
  or or_10 (WBPCplus4, isJalr_out, isUJtype);
  assign WBSel = demultiplexer_19_out1 | demultiplexer_20_out1 | demultiplexer_21_out1;  // OR_Gate or_11, 2 bits wide

  // Other names for the same wires on the sheet: isStype = MemRW

  // Notes on the sheet:
  //   INPUTS to your circuit
  //   done
  //   done
  //   done
  //   BrUn
  //   DON'T CHANGE THE LOCATIONS OF THE INPUTS AND OUTPUTS!
  //   OUTPUT from your circuit
  //   done
  //   done
  //   done
  //   done
  //   ALUSel
  //   done
  //   done
  //   ImmSel
  //   ASel&BSel
  //   MemRW
  //   PCSel
  //   RegWEn
  //   WBSel
endmodule
