// Logisim project cpu.circ as structural Verilog: 1 circuit, main circuit cpu
module cpu (
  input  clk,
  input  [31:0] INSTRUCTION,
  input  [31:0] READ_DATA,
  output [31:0] WRITE_ADDRESS,
  output [31:0] PROGRAM_COUNTER,
  output [31:0] ra,
  output [31:0] sp,
  output [31:0] t0,
  output [31:0] t1,
  output [31:0] t2,
  output [31:0] s0,
  output [31:0] s1,
  output [31:0] a0,
  output [31:0] tohost,
  output [3:0] WRITE_ENABLE,
  output [31:0] WRITE_DATA
);

  wire [2:0] func3, ImmSel;
  wire [31:0] adder_1_out, addi0, extendedImm, IFrest, readdata1, readdata2, thisPC, writeData;

  Adder #(.width(32)) adder_1 (.a(PROGRAM_COUNTER), .b(32'h4), .out(adder_1_out));  // open: cin, cout
  Register #(.width(32)) PC (.D(adder_1_out), .clk(clk), .Q(PROGRAM_COUNTER));  // open: en, clr
  control_logic control_logic_1 (
    .ImmSel(ImmSel), .inst(INSTRUCTION));  // open: CSRWen, PCSel, RegWEn, BrUn, ASel, BSel, ALUSel, MemRW, WBSel, CSRSel, BrEq, BrLt
  Register #(.width(32)) u_IFrest (
    .D(INSTRUCTION), .clk(clk), .Q({IFrest[31:15], func3, IFrest[11:0]}));  // open: en, clr
  Register #(.width(32)) register_1 (.D(PROGRAM_COUNTER), .clk(clk), .Q(thisPC));  // open: en, clr
  imm_gen imm_gen_1 (.inst({IFrest[31:15], func3, IFrest[11:0]}), .ImmSel(ImmSel), .imm(extendedImm));
  regfile regfile_1 (
    .rs1(IFrest[19:15]), .rs2({5{1'b0}}), .rd(IFrest[11:7]), .Write_Data(writeData), .RegWEn(1'b1),
    .clk(clk), .ra(ra), .sp(sp), .t0(t0), .t1(t1), .t2(t2), .s0(s0), .s1(s1), .a0(a0),
    .Read_Data_1(readdata1), .Read_Data_2(readdata2));
  // csr csr_1: pin names not known; wires that end beside it: tohost
  // branch_comp branch_comp_1: pin names not known
  alu alu_1 (.Result(addi0), .A(readdata1), .B(extendedImm), .ALUSel(4'b0000));
  Multiplexer #(.enable("false"), .width(32)) multiplexer_1 (.in0(addi0), .in1(READ_DATA), .out(writeData), .sel(1'b0));

  // Other names for the same wires on the sheet: opcode[6:0] = IFrest[6:0]; rd[4:0] = IFrest[11:7];
  //   IFrest[14:12] = func3; rs1[4:0] = IFrest[19:15]; imm[11:0] = IFrest[31:20]

  // Notes on the sheet:
  //   IF
  //   Output to IMEM
  //   IMEM (do **NOT** move this)
  //   Inputs from IMEM
  //   Inputs/Outputs for testing. Do **NOT** move these.
  //   ID
  //   Outputs To DMEM
  //   DMEM (do **NOT** move this)
  //   Inputs From DMEM
  //   EXE
endmodule
