// Logisim project imm_gen.circ as structural Verilog: 1 circuit, main circuit imm_gen
module imm_gen (
  input  [31:0] inst,
  input  [2:0] ImmSel,
  output [31:0] imm
);

  wire [31:0] immI, immS, immSB, immUJ;

  Multiplexer #(.enable("false"), .select(3), .width(32)) multiplexer_1 (
    .in0(immI), .in1({inst[31:12], {12{1'b0}}}), .in2(immS), .in6(immSB), .in7(immUJ), .out(imm), .sel(ImmSel));  // open: in3, in4, in5
  assign immI = {{20{inst[31]}}, inst[31:20]};  // Bit_Extender bit_extender_1
  assign immSB = {{19{inst[31]}}, {inst[31], inst[7], inst[30:25], inst[11:8], 1'b0}};  // Bit_Extender bit_extender_2
  assign immS = {{20{inst[31]}}, {inst[31:25], inst[11:7]}};  // Bit_Extender bit_extender_3
  assign immUJ = {{11{inst[31]}}, {inst[31], inst[19:12], inst[20], inst[30:21], 1'b0}};  // Bit_Extender bit_extender_4

  // Other names for the same wires on the sheet: immU[31:12] = inst[31:12]

  // Notes on the sheet:
  //   INPUTS to your circuit
  //   I-type
  //   S-type
  //   SB-type
  //   DON'T CHANGE THE LOCATIONS OF THE INPUTS AND OUTPUTS!
  //   OUTPUT from your circuit
  //   U-type
endmodule
