// Logisim project regfile.circ as structural Verilog: 1 circuit, main circuit regfile
module regfile (
  input  [4:0] rs1,
  input  [4:0] rs2,
  input  [4:0] rd,
  input  [31:0] Write_Data,
  input  RegWEn,
  input  clk,
  output [31:0] ra,
  output [31:0] sp,
  output [31:0] t0,
  output [31:0] t1,
  output [31:0] t2,
  output [31:0] s0,
  output [31:0] s1,
  output [31:0] a0,
  output [31:0] Read_Data_1,
  output [31:0] Read_Data_2
);

  wire write_en0, write_en1, write_en2, write_en3, write_en4, write_en5, write_en6, write_en7, write_en8,
       write_en9, write_en10, write_en11, write_en12, write_en013, write_en13, write_en14, write_en15,
       write_en16, write_en17, write_en18, write_en19, write_en20, write_en21, write_en22, write_en23,
       write_en24, write_en25, write_en26, write_en27, write_en28, write_en29, write_en30, write_en31;
  wire [31:0] reg3, reg4, reg11, reg12, reg13, reg14, reg15, reg16, reg17, reg18, reg19, reg20, reg21, reg22,
       reg23, reg24, reg25, reg26, reg27, reg28, reg29, reg30, reg31, reg32;

  Register #(.width(32)) register_1 (.D(Write_Data), .en(write_en4), .clk(clk), .Q(reg4));  // open: clr
  Register #(.width(32)) register_2 (.D(Write_Data), .en(write_en8), .clk(clk), .Q(s0));  // open: clr
  Register #(.width(32)) register_3 (.D(Write_Data), .en(write_en11), .clk(clk), .Q(reg12));  // open: clr
  Register #(.width(32)) register_4 (.D(Write_Data), .en(write_en16), .clk(clk), .Q(reg16));  // open: clr
  Register #(.width(32)) register_5 (.D(Write_Data), .en(write_en20), .clk(clk), .Q(reg20));  // open: clr
  Register #(.width(32)) register_6 (.D(Write_Data), .en(write_en24), .clk(clk), .Q(reg24));  // open: clr
  Register #(.width(32)) register_7 (.D(Write_Data), .en(write_en28), .clk(clk), .Q(reg28));  // open: clr
  Register #(.width(32)) register_8 (.D(Write_Data), .en(write_en1), .clk(clk), .Q(ra));  // open: clr
  Register #(.width(32)) register_9 (.D(Write_Data), .en(write_en5), .clk(clk), .Q(t0));  // open: clr
  Register #(.width(32)) register_10 (.D(Write_Data), .en(write_en9), .clk(clk), .Q(s1));  // open: clr
  Register #(.width(32)) register_11 (.D(Write_Data), .en(write_en013), .clk(clk), .Q(reg13));  // open: clr
  Register #(.width(32)) register_12 (.D(Write_Data), .en(write_en17), .clk(clk), .Q(reg17));  // open: clr
  Register #(.width(32)) register_13 (.D(Write_Data), .en(write_en21), .clk(clk), .Q(reg21));  // open: clr
  Register #(.width(32)) register_14 (.D(Write_Data), .en(write_en25), .clk(clk), .Q(reg25));  // open: clr
  Register #(.width(32)) register_15 (.D(Write_Data), .en(write_en29), .clk(clk), .Q(reg29));  // open: clr
  Register #(.width(32)) register_16 (.D(Write_Data), .en(write_en2), .clk(clk), .Q(sp));  // open: clr
  Register #(.width(32)) register_17 (.D(Write_Data), .en(write_en6), .clk(clk), .Q(t1));  // open: clr
  Register #(.width(32)) register_18 (.D(Write_Data), .en(write_en10), .clk(clk), .Q(a0));  // open: clr
  Register #(.width(32)) register_19 (.D(Write_Data), .en(write_en14), .clk(clk), .Q(reg14));  // open: clr
  Register #(.width(32)) register_20 (.D(Write_Data), .en(write_en18), .clk(clk), .Q(reg18));  // open: clr
  Register #(.width(32)) register_21 (.D(Write_Data), .en(write_en22), .clk(clk), .Q(reg22));  // open: clr
  Register #(.width(32)) register_22 (.D(Write_Data), .en(write_en26), .clk(clk), .Q(reg26));  // open: clr
  Register #(.width(32)) register_23 (.D(Write_Data), .en(write_en30), .clk(clk), .Q(reg31));  // open: clr
  Register #(.width(32)) register_24 (.D(Write_Data), .en(write_en3), .clk(clk), .Q(reg3));  // open: clr
  Register #(.width(32)) register_25 (.D(Write_Data), .en(write_en7), .clk(clk), .Q(t2));  // open: clr
  Register #(.width(32)) register_26 (.D(Write_Data), .en(write_en11), .clk(clk), .Q(reg11));  // open: clr
  Register #(.width(32)) register_27 (.D(Write_Data), .en(write_en15), .clk(clk), .Q(reg15));  // open: clr
  Register #(.width(32)) register_28 (.D(Write_Data), .en(write_en19), .clk(clk), .Q(reg19));  // open: clr
  Register #(.width(32)) register_29 (.D(Write_Data), .en(write_en23), .clk(clk), .Q(reg23));  // open: clr
  Register #(.width(32)) register_30 (.D(Write_Data), .en(write_en27), .clk(clk), .Q(reg27));  // open: clr
  Register #(.width(32)) register_31 (.D(Write_Data), .en(write_en31), .clk(clk), .Q(reg32));  // open: clr
  Demultiplexer #(.enable("false"), .select(5)) demultiplexer_1 (
    .out0(write_en0), .out1(write_en1), .out2(write_en2), .out3(write_en3), .out4(write_en4),
    .out5(write_en5), .out6(write_en6), .out7(write_en7), .out8(write_en8), .out9(write_en9),
    .out10(write_en10), .out11(write_en11), .out12(write_en12), .out13(write_en13), .out14(write_en14),
    .out15(write_en15), .out16(write_en16), .out17(write_en17), .out18(write_en18), .out19(write_en19),
    .out20(write_en20), .out21(write_en21), .out22(write_en22), .out23(write_en23), .out24(write_en24),
    .out25(write_en25), .out26(write_en26), .out27(write_en27), .out28(write_en28), .out29(write_en29),
    .out30(write_en30), .out31(write_en31), .in(RegWEn), .sel(rd));
  Multiplexer #(.enable("false"), .select(5), .width(32)) multiplexer_1 (
    .in0({32{1'b0}}), .in1(ra), .in2(sp), .in3(reg3), .in4(reg4), .in5(t0), .in6(t1), .in7(t2), .in8(s0),
    .in9(s1), .in10(a0), .in11(reg11), .in12(reg12), .in13(reg13), .in14(reg14), .in15(reg15), .in16(reg16),
    .in17(reg17), .in18(reg18), .in19(reg19), .in20(reg20), .in21(reg21), .in22(reg22), .in23(reg23),
    .in24(reg24), .in25(reg25), .in26(reg26), .in27(reg27), .in28(reg28), .in29(reg29), .in30(reg30),
    .in31(reg31), .out(Read_Data_1), .sel(rs1));
  Multiplexer #(.enable("false"), .select(5), .width(32)) multiplexer_2 (
    .in0({32{1'b0}}), .in1(ra), .in2(sp), .in3(reg3), .in4(reg4), .in5(t0), .in6(t1), .in7(t2), .in8(s0),
    .in9(s1), .in10(a0), .in11(reg11), .in12(reg12), .in13(reg13), .in14(reg14), .in15(reg15), .in16(reg16),
    .in17(reg17), .in18(reg18), .in19(reg19), .in20(reg20), .in21(reg21), .in22(reg22), .in23(reg23),
    .in24(reg24), .in25(reg25), .in26(reg26), .in27(reg27), .in28(reg28), .in29(reg29), .in30(reg30),
    .in31(reg31), .out(Read_Data_2), .sel(rs2));

  // Other names for the same wires on the sheet: read_data1[31:0] = Read_Data_1; read_data2[31:0] = Read_Data_2;
  //   read_reg1[4:0] = rs1; read_reg2[4:0] = rs2; reg1[31:0] = ra; reg2[31:0] = sp; reg5[31:0] = t0; reg6[31:0] = t1;
  //   reg7[31:0] = t2; reg8[31:0] = s0; reg9[31:0] = s1; reg10[31:0] = a0; write_en = RegWEn; write_reg[4:0] = rd

  // Notes on the sheet:
  //   INPUTS to your circuit
  //   DON'T CHANGE THE LOCATIONS OF THE INPUTS AND OUTPUTS!
  //   These are DEBUG/TEST outputs from your circuit.
  //   OUTPUTS from your circuit
endmodule
